# Fritzing sketch wiring sketch (saved by Fritzing 0.9.3b)

parts:
  Part1 = Arduino Uno (Rev3) - ICSP
  U1 = SUP500F [package=sup500f]
  M1 = Dagu DGServo 9g (Top view) [part_number=RS001B]  # not connected
  Part2 = LSM303 Breakout Board - Tilt-Compensated Compass

nets:
  N1: Part1.A4/SDA, Part2.SDA_M
  N2: Part1.A5/SCL, Part2.SCL_M
  N3: Part1.D0/RX, U1.TX-O
  N4: Part1.D1/TX, U1.RX-I
